// Logisim project ARITMÉTICA 3 BITS.circ as structural Verilog: 1 circuit, main circuit main
// ARITMÉTICA
module main (
  input  Cin,
  input  S_0,
  input  S_1,
  input  A_0,
  input  B_0,
  input  A_1,
  input  B_1,
  input  A_2,
  input  B_2,
  output Q_0,
  output Q_1,
  output Q_2,
  output C_2,
  output Cout
);

  wire _1_out, main_1_y, main_2_cout;

  not _1 (_1_out, Cin);
  MUX_3_X_1_main main_1 (.E_1(S_0), .E_2(Cin), .E_3(_1_out), .S_0(S_0), .S_1(S_1), .Y(main_1_y));
  SST_main main_2 (.A(A_0), .B(B_0), .Q(Q_0), .Cin(main_1_y), .Cout(main_2_cout), .S(S_0));
  SST_main main_3 (.A(A_1), .B(B_1), .Q(Q_1), .Cin(main_2_cout), .Cout(C_2), .S(S_0));
  SST_main main_4 (.A(A_2), .B(B_2), .Q(Q_2), .Cin(C_2), .Cout(Cout), .S(S_0));
endmodule
