// Logisim project BIT A BIT.circ as structural Verilog: 1 circuit, main circuit main
// BIT
module main (
  input  A,
  input  B,
  output NAND,
  output NOR,
  output XOR
);

  nand u_NAND (NAND, A, B);
  nor u_NOR (NOR, A, B);
  xor u_XOR (XOR, A, B);
endmodule
