// Logisim project DESLOCAMENTO 3 BITS.circ as structural Verilog: 1 circuit, main circuit main
// DESL
module main (
  input  D_2,
  input  D_1,
  input  D_0,
  input  S_0,
  input  S_1,
  output Y_2,
  output Y_1,
  output Y_0
);

  wire main_1_dy_meio, main_1_not_s1, main_1_s1, main_2_dy_anterior, \main_2_dy_próximo , main_2_not_s1_2,
       main_3_dy_meio_2;

  FIM_main main_1 (
    .S_0(S_0), .S_1(S_1), .D_2(D_2), .Y_2(Y_2), .S1(main_1_s1), .NOT_S1(main_1_not_s1),
    .YD_MEIO(\main_2_dy_próximo ), .DY_MEIO(main_1_dy_meio));
  MEIO_main main_2 (
    .S1(main_1_s1), .NOT_S1(main_1_not_s1), .\DY_PRÓXIMO (\main_2_dy_próximo ),
    .\YD_PRÓXIMO (main_1_dy_meio), .D_1(D_1), .Y_1(Y_1), .NOT_S1_2(main_2_not_s1_2),
    .DY_ANTERIOR(main_2_dy_anterior), .YD_ANTERIOR(main_3_dy_meio_2));  // open: S1_2
  \INÍCIO_main  main_3 (
    .NOT_S1(main_2_not_s1_2), .DY_MEIO(main_2_dy_anterior), .DY_MEIO_2(main_3_dy_meio_2), .D_0(D_0), .Y_0(Y_0));
endmodule
