// Logisim project FIM.circ as structural Verilog: 1 circuit, main circuit main
// FIM
module main (
  input  D_2,
  input  S_0,
  input  S_1,
  input  YD_MEIO,
  output S1,
  output NOT_S1,
  output DY_MEIO,
  output Y_2
);

  wire _2_out;

  not _1 (NOT_S1, S_1);
  and _2 (_2_out, S_1, S_0, D_2);
  or _4 (Y_2, _2_out, YD_MEIO);
  and _3 (DY_MEIO, D_2, S_1);

  assign S1 = S_1;
endmodule
