// Logisim project INÍCIO.circ as structural Verilog: 1 circuit, main circuit main
// INIC
module main (
  input  D_0,
  input  NOT_S1,
  input  DY_MEIO,
  output DY_MEIO_2,
  output Y_0
);

  and _1 (DY_MEIO_2, NOT_S1, D_0);

  assign Y_0 = DY_MEIO;
endmodule
