// Logisim project MEIO.circ as structural Verilog: 1 circuit, main circuit main
// MEIO
module main (
  input  D_1,
  input  S1,
  input  NOT_S1,
  input  \YD_PRÓXIMO ,
  input  YD_ANTERIOR,
  output S1_2,
  output NOT_S1_2,
  output DY_ANTERIOR,
  output \DY_PRÓXIMO ,
  output Y_1
);

  and _1 (\DY_PRÓXIMO , NOT_S1, D_1);
  or _3 (Y_1, \YD_PRÓXIMO , YD_ANTERIOR);
  and _2 (DY_ANTERIOR, D_1, S1);

  assign NOT_S1_2 = NOT_S1;
  assign S1_2 = S1;
endmodule
