// Logisim project MUX 4 X 1 3 BITS.circ as structural Verilog: 1 circuit, main circuit main
// MUX 4 X 1
module main (
  input  E_2,
  input  E_1,
  input  E_0,
  input  C_2,
  input  C_1,
  input  C_0,
  input  B_2,
  input  B_1,
  input  B_0,
  input  A_2,
  input  A_1,
  input  A_0,
  input  S_1,
  input  S_0,
  output Y_2,
  output Y_1,
  output Y_0
);

  // MUX_4_X_1_main main_1: pin names not known; wires that end beside it: E_2, C_2, B_2, Y_2, A_2, S_1, S_0
  // MUX_4_X_1_main main_2: pin names not known; wires that end beside it: E_1, C_1, B_1, Y_1, A_1, S_1, S_0
  // MUX_4_X_1_main main_3: pin names not known; wires that end beside it: E_0, C_0, B_0, Y_0, A_0, S_1, S_0
endmodule
