// Logisim project XOR 3 BITS.circ as structural Verilog: 1 circuit, main circuit main
// XOR
module main (
  input  S_2,
  input  E_0,
  input  E_1,
  input  E_2,
  output Y_0,
  output Y_1,
  output Y_2
);

  xor _1 (Y_0, E_0, S_2);
  xor _2 (Y_1, E_1, S_2);
  xor _3 (Y_2, E_2, S_2);
endmodule
